# Fritzing sketch circuit (saved by Fritzing 0.9.3b)
breadboards: 1

parts:
  U1 = ATTINY13 [package=dip]
  DHT1 = DHT11 Humitidy and Temperature Sensor
  R1 = Resistor [tolerance=±5% resistance=10k package=THT]
  BAT1 = Battery Holders [package=battcon_245mm_pth]
  Part1 = NRF24L01+ Breakout Board
  R2 = Resistor [tolerance=±5% resistance=4.7k package=THT]
  R3 = Resistor [tolerance=±5% resistance=220 package=THT]
  C2 = Ceramic Capacitor [capacitance=1µF package="100 mil [THT, multilayer]"]

nets:
  dht11: U1.PB3(ADC3), DHT1.DATA, R1.Pin_1
  GND: U1.GND, DHT1.GND, BAT1.-, Part1.GND, C2.0
  MIMO: U1.PB0(MOSI), Part1.MOSI, R2.Pin_1
  sck: U1.PB2(SCK_ADC1), Part1.SCK, R3.Pin_0
  3V: U1.VCC, DHT1.VDD, R1.Pin_0, BAT1.+, Part1.VCC, Part1.CE
  N1: Part1.CS, R3.Pin_1, C2.1
  N2: Part1.MISO, R2.Pin_0

custom parts:
  DHT11 Humitidy and Temperature Sensor: DHT11 Humidity and Temperature Sensor
